# Fritzing sketch duckveloper (saved by Fritzing 0.9.4)
breadboards: 1

parts:
  (Mounted_on_Arduino) = Arduino MP3 Player Shield
  Button = Pushbutton [package="[THT]"]
  R3 = Resistor [tolerance=±5% resistance=10k package=THT]
  LED1 = smd LED [color="Red (633nm)" package="0603 [SMD]"]
  R2 = Resistor [tolerance=±5% resistance=330 package=THT]
  SP1 = SPEAKER [package=pcb_mount_speaker]
  (Follow_the_Sparkfun_Mono_Audio_Amplifier_Quickstart_Guide) = TPA2000D1 Audio Amplifier [package="Breakout board Double Row DIL16"]

nets:
  N1: (Mounted_on_Arduino).GBUF, (Follow_the_Sparkfun_Mono_Audio_Amplifier_Quickstart_Guide).INN
  N2: (Mounted_on_Arduino).RIGHT, (Follow_the_Sparkfun_Mono_Audio_Amplifier_Quickstart_Guide).INP
  N3: (Mounted_on_Arduino).VCC, Button.Pin_3, Button.Pin_4
  N4: (Mounted_on_Arduino).D5, Button.Pin_2, R3.Pin_0
  N5: (Mounted_on_Arduino).5V-MP3-CS, LED1.anode
  N6: (Mounted_on_Arduino).5V-MOSI, (Follow_the_Sparkfun_Mono_Audio_Amplifier_Quickstart_Guide).PVDD
  GND: (Mounted_on_Arduino).GND, R3.Pin_1, R2.Pin_1, (Follow_the_Sparkfun_Mono_Audio_Amplifier_Quickstart_Guide).GND
  N7: LED1.cathode, R2.Pin_0
  N8: SP1.+, (Follow_the_Sparkfun_Mono_Audio_Amplifier_Quickstart_Guide).OUTP
  N9: SP1.-, (Follow_the_Sparkfun_Mono_Audio_Amplifier_Quickstart_Guide).OUTN
